# Fritzing sketch Schematic (saved by Fritzing 1.0.1rc)
breadboards: 1

parts:
  Part1 = Arduino Nano (Rev3.0)
  LED1 = smd LED [color="Red (633nm)" package="1206 [SMD]"]
  S1 = Taiway 100-SP-X-T1 SPDT Miniature Toggle Switch [part_number=100-SP-X-T1-0-0-B1-M2 package=THT]

nets:
  N1: Part1.GND, S1.L1
  N2: Part1.D4, LED1.anode
  N3: Part1.D5, S1.L2
